# Fritzing sketch circuit solaire v11 definitif (saved by Fritzing 1.0.6)
breadboards: 1

parts:
  Panneau_Solaire_12V = Solar Panel [package="Renogy 50 Watts 12 Volt Monocrystalline Bendable Solar Panel"]
  Batterie_6V = 6v battery [package=battery]
  R1_10kΩ = Resistor [resistance=10k tolerance=±5% package="2010 [SMD]"]
  R2_3_3kΩ = Resistor [resistance=3.3k tolerance=±5% package="2010 [SMD]"]
  ADS1115_ADC = Adafruit ADS1115 16Bit I2C ADC [part_number="Adafruit #1085"]
  Raspberry_Pi_4B = Adafruit T-Cobbler Plus [part_number="Adafruit #1989 and #2028"]
  ULN2003A_Moteur_1 = ULN2003A - Stepper Driver Board [package=board]
  ULN2003A_Moteur_2 = ULN2003A - Stepper Driver Board [package=board]
  SM1_Moteur_1 = 28BYJ-48 Stepper Motor [part_number=28BYJ-48]
  SM2_Moteur_2 = 28BYJ-48 Stepper Motor [part_number=28BYJ-48]
  LED1_Rouge = smd LED [color="Red (633nm)" package="0805 [SMD]"]
  K1_Relais_5V = Relay [part_number=FRS1B-S package=THT]

nets:
  VCC: Panneau_Solaire_12V.Connector_1, Batterie_6V.+, R1_10kΩ.Pin_0, R1_10kΩ.Pin_1, R2_3_3kΩ.Pin_0, ADS1115_ADC.AIN1, Raspberry_Pi_4B.GPIO17, Raspberry_Pi_4B.+5V, ULN2003A_Moteur_1.VCC, ULN2003A_Moteur_2.VCC, K1_Relais_5V.A, K1_Relais_5V.C1, K1_Relais_5V.C2
  GND: Panneau_Solaire_12V.Connector_2, Batterie_6V.-, R2_3_3kΩ.Pin_1, ADS1115_ADC.GND, Raspberry_Pi_4B.GND, ULN2003A_Moteur_1.GND, ULN2003A_Moteur_2.GND, LED1_Rouge.anode, K1_Relais_5V.COIL1
  N1: Raspberry_Pi_4B.GPIO22, ULN2003A_Moteur_2.IN1
  N2: Raspberry_Pi_4B.GPIO5, ULN2003A_Moteur_1.IN1
  N3: Raspberry_Pi_4B.GPIO6, ULN2003A_Moteur_1.IN2
  N4: Raspberry_Pi_4B.GPIO13, ULN2003A_Moteur_1.IN3
  N5: Raspberry_Pi_4B.GPIO19, ULN2003A_Moteur_1.IN4
  N6: Raspberry_Pi_4B.GPIO18, LED1_Rouge.cathode
  N7: Raspberry_Pi_4B.GPIO23, ULN2003A_Moteur_2.IN2
  N8: Raspberry_Pi_4B.GPIO24, ULN2003A_Moteur_2.IN3
  N9: Raspberry_Pi_4B.GPIO25, ULN2003A_Moteur_2.IN4
  N10: ULN2003A_Moteur_1.BLUE, SM1_Moteur_1.blue-pin
  N11: ULN2003A_Moteur_1.PINK, SM1_Moteur_1.pink-pin
  N12: ULN2003A_Moteur_1.YELLOW, SM1_Moteur_1.yellow-pin
  N13: ULN2003A_Moteur_1.ORANGE, SM1_Moteur_1.orange-pin
  N14: ULN2003A_Moteur_1.RED, SM1_Moteur_1.red-pin
  N15: ULN2003A_Moteur_2.BLUE, SM2_Moteur_2.blue-pin
  N16: ULN2003A_Moteur_2.PINK, SM2_Moteur_2.pink-pin
  N17: ULN2003A_Moteur_2.YELLOW, SM2_Moteur_2.yellow-pin
  N18: ULN2003A_Moteur_2.ORANGE, SM2_Moteur_2.orange-pin
  N19: ULN2003A_Moteur_2.RED, SM2_Moteur_2.red-pin
  N20: ULN2003A_Moteur_2.B, ULN2003A_Moteur_2.E

custom parts:
  Solar Panel: Renogy 50 Watts 12 Volt Solar Panel
  6v battery: 6V lead acid battery 12ah
  Adafruit ADS1115 16Bit I2C ADC: For microcontrollers without an analog-to-digital converter or when you want a higher-precision ADC, the ADS1115 provides 16-bit precision at 860 samples/second over I2C. The chip can be configured as 4 single-ended input channels, or two differential channels. As a nice bonus, it even includes a programmable gain amplifier, up to x16, to help boost up smaller single/differential signals to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
  Adafruit T-Cobbler Plus: The Raspberry Pi has landed on the Maker World like a 40-GPIO pinned, quad-USB ported, credit card sized bomb of DIY joy. And while you can use most of our great Model B accessories by hooking up our downgrade cable, its probably a good time to upgrade your set up and accessorize using all of the 40 pins. That's why we now carry the Assembled Adafruit Pi T-Cobbler Plus - Breakout + Cable for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
  ULN2003A - Stepper Driver Board: A common stepper motor driver board based on ULN2003APG darlington array
  28BYJ-48 Stepper Motor: Unipolar Stepper Motor 28BYJ-48 Top coil - pink & orange Bottom coil - blue & yellow Common rail - red Connector pins: blue - pink - yellow - orange - red
